# Fritzing sketch uss-1k-2k-rpi-2 (saved by Fritzing 0.9.3b)
breadboards: 1

parts:
  Raspberry_Pi_1 = Raspberry Pi 3 [part_number=RPI-3-V1.2]
  hc-sr1 = hc-sr04
  R2 = Resistor [tolerance=±5% resistance=1k package=THT]
  R3 = Resistor [tolerance=±20% resistance=220 package="2512 [SMD]"]  # not connected
  R1 = Resistor [tolerance=±5% resistance=2k package="2512 [SMD]"]  # not connected

nets:
  N1: Raspberry_Pi_1.GIPO4, hc-sr1.Trig
  N2: Raspberry_Pi_1.GIPO17, R2.Pin_0
  GND: Raspberry_Pi_1.GND, hc-sr1.GND
  5V: Raspberry_Pi_1.5V, hc-sr1.VCC
  N3: hc-sr1.Echo, R2.Pin_1
